// Logisim project masterSlaveJK.circ as structural Verilog: 1 circuit, main circuit main
module main (
  input  J,
  input  in_2,
  input  in_3,
  input  K,
  output Q,
  output Q_prime
);

  wire Clock_out, nand_1_out, nand_2_out, nand_3_out, nand_4_out, nand_5_out, nand_6_out, nand_7_out,
       nand_8_out, nand_9_out, nand_10_out, nand_11_out;

  Clock Clock (.out(Clock_out));
  nand nand_1 (nand_1_out, J, Clock_out);
  nand nand_2 (nand_2_out, Clock_out, K);
  nand nand_3 (nand_3_out, Q_prime, nand_4_out);
  nand nand_4 (nand_4_out, nand_1_out, nand_1_out);
  nand nand_5 (nand_5_out, nand_2_out, nand_2_out);
  nand nand_6 (nand_6_out, nand_5_out, Q);
  nand nand_7 (nand_7_out, nand_3_out, nand_8_out);
  nand nand_8 (nand_8_out, nand_7_out, nand_6_out);
  nand nand_9 (nand_9_out, Clock_out, Clock_out);
  nand nand_10 (nand_10_out, nand_7_out, nand_9_out);
  nand nand_11 (nand_11_out, nand_9_out, nand_8_out);
  nand nand_12 (Q, nand_10_out, Q_prime);
  nand nand_13 (Q_prime, Q, nand_11_out);
endmodule
