// Logisim project masterSlaveJK_IC.circ as structural Verilog: 1 circuit, main circuit main
module main (
  input  Initial_input,
  input  J,
  input  K,
  output Q,
  output Q_prime
);

  wire Clock_out, n7400_1_p2, n7400_1_p3, n7400_1_p11, n7400_2_p2, n7400_2_p5, n7410_1_p6, n7410_1_p10;

  Clock Clock (.out(Clock_out));
  // _7410 7410_1: pin names not known; wires that end beside it: J, Clock_out, Clock_out, K, Q, n7410_1_p6, 1'b0, 1'b1, Q_prime, n7410_1_p10, Initial_input
  // _7400 7400_1: pin names not known; wires that end beside it: n7410_1_p10, n7400_1_p2, n7400_1_p3, n7400_1_p3, n7410_1_p6, n7400_1_p2, 1'b0, 1'b1, Clock_out, Clock_out, n7400_1_p11
  // _7400 7400_2: pin names not known; wires that end beside it: n7400_1_p11, n7400_2_p2, n7400_1_p11, n7400_1_p2, n7400_2_p5, 1'b0, n7400_1_p3, 1'b1, n7400_2_p2, Q_prime, Q, Q, n7400_2_p5, Q_prime
endmodule
