// Logisim project Sec_A1_Group_5_Problem_1.circ as structural Verilog: 1 circuit, main circuit main
module main (
  input  J,
  input  in_2,
  input  K,
  output Q,
  output Q_prime
);

  wire Clock_out, n7400_1_p3, n7400_1_p6, n7400_1_p11, n7400_1_p13, n7400_1_p14, n7400_2_p1, n7400_2_p3,
       n7400_2_p10, n7400_3_p2, n7400_3_p3, n7400_4_p6;

  Clock Clock (.out(Clock_out));
  // _7400 7400_1: pin names not known; wires that end beside it: J, Clock_out, n7400_1_p3, n7400_1_p3, n7400_1_p3, n7400_1_p6, 1'b0, 1'b1, n7400_1_p6, Q_prime, n7400_1_p11, n7400_1_p11, n7400_1_p13, n7400_1_p14, in_2
  // _7400 7400_2: pin names not known; wires that end beside it: n7400_2_p1, n7400_2_p1, n7400_2_p3, Clock_out, K, n7400_2_p1, 1'b0, 1'b1, n7400_1_p14, n7400_2_p10, n7400_1_p13, Q, n7400_2_p3, n7400_2_p10
  // _7400 7400_3: pin names not known; wires that end beside it: n7400_1_p14, n7400_3_p2, n7400_3_p3, 1'b0, 1'b1, n7400_3_p3, Q_prime, Q
  // _7400 7400_4: pin names not known; wires that end beside it: Clock_out, Clock_out, n7400_3_p2, n7400_3_p2, n7400_1_p13, n7400_4_p6, 1'b0, 1'b1, Q, n7400_4_p6, Q_prime
endmodule
