// Logisim project Sec_A1_Group_5_Problem_2.circ as structural Verilog: 2 circuits, main circuit main
module main (
  input  C_P,
  input  RS,
  input  LS,
  input  S1,
  input  S0,
  input  I3,
  input  I2,
  input  I1,
  input  I0,
  output A3,
  output A2,
  output A1,
  output A0
);

  wire Clock_out, mux_1_y, mux_3_y, n7474_1_p9, n7474_2_p9;

  Clock Clock (.out(Clock_out));
  MUX mux_1 (.S1(S1), .S0(S0), .Y(mux_1_y), .A3(I3), .A2(A2), .A1(RS), .A0(A3));
  // _7474 7474_1: pin names not known; wires that end beside it: C_P, mux_1_y, Clock_out, C_P, A3, 1'b0, 1'b1, C_P, n7474_1_p9, Clock_out, C_P, A2
  MUX mux_2 (.S1(S1), .S0(S0), .Y(n7474_1_p9), .A3(I2), .A2(A1), .A1(A3), .A0(A2));
  MUX mux_3 (.S1(S1), .S0(S0), .Y(mux_3_y), .A3(I1), .A2(A0), .A1(A2), .A0(A1));
  // _7474 7474_2: pin names not known; wires that end beside it: C_P, mux_3_y, Clock_out, C_P, A1, 1'b0, 1'b1, C_P, n7474_2_p9, Clock_out, C_P, A0
  MUX mux_4 (.S1(S1), .S0(S0), .Y(n7474_2_p9), .A3(I0), .A2(LS), .A1(A1), .A0(A0));
endmodule

module MUX (
  input  S1,
  input  S0,
  input  A3,
  input  A2,
  input  A1,
  input  A0,
  output Y
);

  wire n7404_1_p2, n7404_1_p6, n7408_1_p3, n7408_1_p9, n7408_2_p5, n7408_2_p13, n7432_1_p1, n7432_1_p2,
       n7432_1_p3, n7432_1_p5, n7432_1_p6, n7432_1_p8;

  // _7404 7404_1: pin names not known; wires that end beside it: S1, n7404_1_p2, 1'b0, 1'b1, S0, n7404_1_p6
  // _7432 7432_1: pin names not known; wires that end beside it: n7432_1_p1, n7432_1_p2, n7432_1_p3, n7432_1_p3, n7432_1_p5, n7432_1_p6, n7432_1_p6, n7432_1_p8, Y
  // _7408 7408_1: pin names not known; wires that end beside it: S1, S0, n7408_1_p3, n7408_1_p3, A3, 1'b1, S1, n7404_1_p6, n7408_1_p9, n7408_1_p9
  // _7408 7408_2: pin names not known; wires that end beside it: n7432_1_p2, 1'b0, n7404_1_p2, S0, n7408_2_p5, n7408_2_p5, A1, n7432_1_p1, A2, n7432_1_p5, n7404_1_p6, n7404_1_p2, n7408_2_p13, n7408_2_p13, A0, n7432_1_p8
endmodule
