// Logisim project Up counter.circ as structural Verilog: 1 circuit, main circuit main
module main (
  output y3,
  output y2,
  output y1,
  output y0
);

  wire clock_1_out, n7408_1_p3, n7408_1_p5, n7408_2_p3, n7408_2_p6, n7408_2_p11, n7476_1_p12;

  Clock clock_1 (.out(clock_1_out));
  // _7408 7408_1: pin names not known; wires that end beside it: 1'b0, 1'b1, n7408_1_p3, y3, n7408_1_p5
  // _7476 7476_1: pin names not known; wires that end beside it: clock_1_out, n7408_1_p5, 1'b1, 1'b1, clock_1_out, n7408_1_p5, 1'b1, y0, 1'b0, y0, y1, n7476_1_p12, y0
  // _7408 7408_2: pin names not known; wires that end beside it: y1, y0, n7408_2_p3, n7408_2_p3, y2, n7408_2_p6, 1'b0, 1'b1, y0, n7476_1_p12, n7408_2_p11, n7408_2_p11, y2, n7408_1_p3
  // _7476 7476_2: pin names not known; wires that end beside it: clock_1_out, n7408_1_p5, n7408_2_p3, 1'b1, clock_1_out, n7408_1_p5, n7408_2_p3, y2, 1'b0, n7408_2_p6, y3, n7408_2_p6
endmodule
