// Logisim project 2 bit counter.circ as structural Verilog: 1 circuit, main circuit main
module main (
  input  in_1,
  output y1,
  output y0
);

  wire clock_1_out;

  Clock clock_1 (.out(clock_1_out));
  // _7476 7476_1: pin names not known; wires that end beside it: clock_1_out, in_1, clock_1_out, in_1, y0, y0, y1, y0
endmodule
