// Logisim project 4 bit counter with 2 2 bit.circ as structural Verilog: 1 circuit, main circuit main
module main (
  input  in_1,
  input  in_2,
  output y4,
  output y3,
  output y2,
  output y1
);

  wire and_1_out, clock_2_out, j_k_ff_1_qn, j_k_ff_2_qn;

  Clock clock_1 ();  // open: out
  Clock clock_2 (.out(clock_2_out));
  J_K_Flip_Flop j_k_ff_1 (
    .J(in_1), .clk(clock_2_out), .K(in_1), .Q(y1), .Qn(j_k_ff_1_qn), .en(in_1));  // open: preset, reset
  J_K_Flip_Flop j_k_ff_2 (
    .J(y1), .clk(clock_2_out), .K(y1), .Q(y2), .Qn(j_k_ff_2_qn), .en(in_1));  // open: preset, reset
  and and_1 (and_1_out, j_k_ff_1_qn, j_k_ff_2_qn, clock_2_out);
  J_K_Flip_Flop j_k_ff_3 (.J(in_2), .clk(and_1_out), .K(in_2), .Q(y3), .en(in_2));  // open: Qn, preset, reset
  J_K_Flip_Flop j_k_ff_4 (.J(y3), .clk(and_1_out), .K(y3), .Q(y4), .en(in_1));  // open: Qn, preset, reset
endmodule
