// Logisim project Up Down.circ as structural Verilog: 2 circuits, main circuit main
module main (
  input  in_1,
  input  Up_1__Down_0,
  output y3,
  output y2,
  output y1,
  output y0
);

  wire clock_1_out, n7476_1_p1, n7476_1_p3, n7476_2_p1;

  Clock clock_1 (.out(clock_1_out));
  // _7476 7476_1: pin names not known; wires that end beside it: n7476_1_p1, in_1, n7476_1_p3, in_1, y3, in_1, y2, in_1
  // _7476 7476_2: pin names not known; wires that end beside it: n7476_2_p1, in_1, clock_1_out, in_1, y1, in_1, y0, in_1
  // _7486 7486_1: pin names not known; wires that end beside it: y2, Up_1__Down_0, n7476_1_p1, y0, Up_1__Down_0, n7476_2_p1, Up_1__Down_0, y1, n7476_1_p3
endmodule

module basic (
  input  in_1,
  input  Up_1__Down_0,
  output y3,
  output y2,
  output y1,
  output y0
);

  wire clock_1_out, n7408_1_p1, n7408_1_p3, n7408_1_p5, n7408_1_p6, n7408_2_p1, n7408_2_p7, n7432_1_p4,
       n7432_1_p5, n7432_1_p7, n7432_1_p8, n7432_1_p9, n7476_1_p1, n7476_1_p3;

  Clock clock_1 (.out(clock_1_out));
  // _7408 7408_1: pin names not known; wires that end beside it: n7408_1_p1, Up_1__Down_0, n7408_1_p3, y2, n7408_1_p5, n7408_1_p6
  // _7476 7476_1: pin names not known; wires that end beside it: n7476_1_p1, in_1, n7476_1_p3, in_1, y3, in_1, y2, n7408_1_p1, in_1
  // _7432 7432_1: pin names not known; wires that end beside it: n7408_1_p3, n7408_1_p6, n7476_1_p1, n7432_1_p4, n7432_1_p5, n7476_1_p3, n7432_1_p7, n7432_1_p8, n7432_1_p9
  // _7408 7408_2: pin names not known; wires that end beside it: n7408_2_p1, Up_1__Down_0, n7432_1_p5, y1, n7408_1_p5, n7432_1_p4, n7408_2_p7, Up_1__Down_0, n7432_1_p8, y0, n7408_1_p5, n7432_1_p7
  // _7476 7476_2: pin names not known; wires that end beside it: n7432_1_p9, in_1, clock_1_out, in_1, y1, n7408_2_p1, in_1, y0, n7408_2_p7, in_1
  // _7404 7404_1: pin names not known; wires that end beside it: Up_1__Down_0, n7408_1_p5
endmodule
