// Logisim project Up counter.circ as structural Verilog: 1 circuit, main circuit main
module main (
  input  in_1,
  output y3,
  output y2,
  output y1,
  output y0,
  output out_6,
  output out_7,
  output out_8,
  output out_9
);

  wire clock_1_out;

  Clock clock_1 (.out(clock_1_out));
  // _7476 7476_1: pin names not known; wires that end beside it: clock_1_out, in_1, out_9, in_1, y0, out_9, in_1, y1, out_8, in_1
  // _7476 7476_2: pin names not known; wires that end beside it: out_8, in_1, out_7, in_1, y2, out_7, in_1, y3, out_6, in_1, in_1
endmodule
