// Logisim project modulo 5.circ as structural Verilog: 2 circuits, main circuit main
module main (
  input  in_1,
  output out_2,
  output out_3,
  output out_4
);

  wire and_1_out, clock_1_out, j_k_ff_1_qn, j_k_ff_2_qn;

  Clock clock_1 (.out(clock_1_out));
  J_K_Flip_Flop j_k_ff_1 (
    .J(in_1), .clk(clock_1_out), .K(in_1), .Q(out_4), .Qn(j_k_ff_1_qn), .reset(and_1_out));  // open: preset, en
  J_K_Flip_Flop j_k_ff_2 (
    .J(in_1), .clk(j_k_ff_1_qn), .K(in_1), .Q(out_3), .Qn(j_k_ff_2_qn), .reset(and_1_out));  // open: preset, en
  J_K_Flip_Flop j_k_ff_3 (.J(in_1), .clk(j_k_ff_2_qn), .K(in_1), .Q(out_2), .reset(and_1_out));  // open: Qn, preset, en
  and and_1 (and_1_out, out_2, ~out_3, out_4);  // AND_Gate
endmodule

module IC (
  input  in_1,
  output out_2,
  output out_3,
  output out_4
);

  wire clock_1_out, n7408_1_p3, n7476_1_p2, n7476_1_p4, n7476_1_p11, n7476_2_p4;

  Clock clock_1 (.out(clock_1_out));
  // _7476 7476_1: pin names not known; wires that end beside it: clock_1_out, n7476_1_p2, in_1, n7476_1_p4, n7476_1_p2, in_1, out_4, n7476_1_p4, in_1, out_3, n7476_1_p11, in_1
  // _7476 7476_2: pin names not known; wires that end beside it: n7476_1_p11, n7476_1_p2, in_1, n7476_2_p4, in_1, out_2, in_1, n7476_2_p4, in_1
  // _7408 7408_1: pin names not known; wires that end beside it: out_2, out_4, n7408_1_p3, n7408_1_p3, n7476_1_p11, n7476_1_p2, in_1
endmodule
