// Logisim project 1805022.circ as structural Verilog: 1 circuit, main circuit main
module main (
  input  in_1,
  output Y2,
  output Y1,
  output Y0
);

  wire clock_1_out, n7432_1_p4, n7476_1_p7, n7476_1_p9, n7476_1_p11;

  Clock clock_1 (.out(clock_1_out));
  // _7476 7476_1: pin names not known; wires that end beside it: clock_1_out, Y2, 1'b1, clock_1_out, Y2, Y0, n7476_1_p7, 1'b0, n7476_1_p9, Y1, n7476_1_p11, n7476_1_p9
  // _7432 7432_1: pin names not known; wires that end beside it: 1'b0, 1'b1, n7476_1_p11, n7432_1_p4, n7476_1_p9
  // _7408 7408_1: pin names not known; wires that end beside it: 1'b0, 1'b1, Y2, n7476_1_p7, n7432_1_p4
  // _7476 7476_2: pin names not known; wires that end beside it: clock_1_out, in_1, 1'b1, in_1, Y2, 1'b0
endmodule
