// Logisim project BCD.circ as structural Verilog: 1 circuit, main circuit main
module main (
  input  in_1,
  output Y3,
  output Y2,
  output Y1,
  output Y0
);

  wire clock_1_out, n7408_1_p1, n7408_1_p2, n7408_1_p6, n7408_1_p8, n7476_1_p2, n7476_1_p7, n7476_1_p10;

  Clock clock_1 (.out(clock_1_out));
  // _7476 7476_1: pin names not known; wires that end beside it: clock_1_out, n7476_1_p2, in_1, clock_1_out, in_1, Y0, n7476_1_p7, n7476_1_p7, Y1, n7476_1_p10, n7476_1_p7
  // _7408 7408_1: pin names not known; wires that end beside it: n7408_1_p1, n7408_1_p2, n7476_1_p2, n7476_1_p10, n7476_1_p7, n7408_1_p6, n7408_1_p6, n7408_1_p8, n7408_1_p2
  // _7476 7476_2: pin names not known; wires that end beside it: clock_1_out, n7476_1_p2, n7408_1_p6, clock_1_out, n7476_1_p2, n7408_1_p6, Y2, n7408_1_p8, n7408_1_p2, Y3, n7408_1_p1, n7408_1_p2, n7476_1_p2
endmodule
