// Logisim project Jonson Counter.circ as structural Verilog
module D_FF (
  input  in_1,
  output Y0,
  output Y0_2,
  output Y0_3,
  output Y0_4
);

  wire clock_1_out, n7474_1_p2;

  Clock clock_1 (.out(clock_1_out));
  // _7474 7474_1: pin names not known; wires that end beside it: in_1, n7474_1_p2, clock_1_out, Y0, in_1, Y0, clock_1_out, Y0_2
  // _7474 7474_2: pin names not known; wires that end beside it: in_1, Y0_2, clock_1_out, Y0_3, in_1, Y0_3, clock_1_out, Y0_4, n7474_1_p2
endmodule
