// Logisim project Sequence Counter.circ as structural Verilog: 1 circuit, main circuit main
module main (
  output Y2,
  output Y1,
  output Y0
);

  wire clock_1_out, n7408_1_p3, n7408_1_p6, n7408_1_p9, n7432_1_p2, n7432_1_p3, n7432_1_p9, n7476_1_p2,
       n7476_1_p6, n7476_1_p7, n7476_1_p9;

  Clock clock_1 (.out(clock_1_out));
  // _7476 7476_1: pin names not known; wires that end beside it: clock_1_out, n7476_1_p2, clock_1_out, n7476_1_p2, Y0, n7476_1_p6, n7476_1_p7, Y1, n7476_1_p9, n7476_1_p7
  // _7408 7408_1: pin names not known; wires that end beside it: n7476_1_p9, n7476_1_p6, n7408_1_p3, n7408_1_p3, Y2, n7408_1_p6, Y0, Y1, n7408_1_p9
  // _7432 7432_1: pin names not known; wires that end beside it: n7408_1_p9, n7432_1_p2, n7432_1_p3, n7408_1_p9, n7408_1_p6, n7476_1_p7, n7432_1_p2, Y1, n7432_1_p9, n7432_1_p9, Y0, n7476_1_p2
  // _7476 7476_2: pin names not known; wires that end beside it: clock_1_out, n7432_1_p3, clock_1_out, n7432_1_p3, Y2, n7432_1_p2
endmodule
