// Logisim project bcd-down Maneesha.circ as structural Verilog: 1 circuit, main circuit main
module main (
  input  in_1,
  output Y3,
  output Y2,
  output Y1,
  output Y0
);

  wire clock_1_out, n7408_1_p3, n7408_1_p6, n7408_1_p9, n7408_1_p11, n7408_1_p12, n7476_1_p6, n7476_1_p9,
       n7476_1_p10;

  Clock clock_1 (.out(clock_1_out));
  // _7476 7476_1: pin names not known; wires that end beside it: clock_1_out, in_1, clock_1_out, in_1, Y0, n7476_1_p6, n7476_1_p6, Y1, n7476_1_p9, n7476_1_p10
  // _7408 7408_1: pin names not known; wires that end beside it: n7476_1_p6, Y2, n7408_1_p3, n7476_1_p6, Y3, n7408_1_p6, n7476_1_p6, n7476_1_p9, n7408_1_p9, n7408_1_p9, n7408_1_p11, n7408_1_p12
  // _7432 7432_1: pin names not known; wires that end beside it: n7408_1_p6, n7408_1_p3, n7476_1_p10
  // _7476 7476_2: pin names not known; wires that end beside it: clock_1_out, n7408_1_p6, clock_1_out, n7408_1_p9, Y2, n7408_1_p11, n7476_1_p6, Y3, n7408_1_p12
endmodule
