// Logisim project bcd-up Maneesha.circ as structural Verilog: 1 circuit, main circuit main
module main (
  input  in_1,
  output out_2,
  output out_3,
  output out_4,
  output out_5
);

  wire clock_1_out, n7408_1_p3, n7408_1_p6, n7408_1_p8, n7476_1_p8;

  Clock clock_1 (.out(clock_1_out));
  // _7476 7476_1: pin names not known; wires that end beside it: clock_1_out, in_1, clock_1_out, in_1, out_5, out_5, out_4, n7476_1_p8
  // _7408 7408_1: pin names not known; wires that end beside it: out_5, out_4, n7408_1_p3, n7408_1_p3, out_3, n7408_1_p6, out_5, n7408_1_p8, n7476_1_p8
  // _7476 7476_2: pin names not known; wires that end beside it: clock_1_out, n7408_1_p3, clock_1_out, n7408_1_p3, out_3, out_5, out_2, n7408_1_p8, n7408_1_p6
endmodule
