// Logisim project Advanced Up Down Counter.circ as structural Verilog: 1 circuit, main circuit main
module main (
  input  X,
  output Y2,
  output Y1,
  output Y0
);

  wire clock_1_out, n7404_1_p2, n7404_1_p4, n7404_1_p6, n7408_2_p3, n7408_2_p6, n7408_2_p9, n7408_2_p12,
       n7432_1_p1, n7432_1_p3, n7432_1_p4, n7432_1_p5, n7432_1_p6, n7432_1_p9, n7432_1_p10, n7432_1_p11,
       n7432_2_p11, n7474_1_p2, n7474_1_p3;

  // _7404 7404_1: pin names not known; wires that end beside it: X, n7404_1_p2, Y1, n7404_1_p4, Y2, n7404_1_p6
  Clock clock_1 (.out(clock_1_out));
  // _7432 7432_1: pin names not known; wires that end beside it: n7432_1_p1, n7404_1_p6, n7432_1_p3, n7432_1_p4, n7432_1_p5, n7432_1_p6, n7404_1_p6, n7404_1_p4, n7432_1_p9, n7432_1_p10, n7432_1_p11, n7432_1_p1
  // _7474 7474_1: pin names not known; wires that end beside it: Y0, n7474_1_p2, n7474_1_p3, clock_1_out, Y0, n7474_1_p2, n7432_1_p3, clock_1_out, Y1, n7404_1_p4
  // _7408 7408_1: pin names not known; wires that end beside it: n7404_1_p2, Y0, n7432_1_p10, X, n7474_1_p2, n7432_1_p11, n7432_1_p11, n7404_1_p6, n7432_1_p4, n7404_1_p2, n7404_1_p4, n7432_1_p5
  // _7474 7474_2: pin names not known; wires that end beside it: n7432_1_p9, clock_1_out, Y2, n7404_1_p6
  // _7408 7408_2: pin names not known; wires that end beside it: X, Y2, n7408_2_p3, n7408_2_p3, Y0, n7408_2_p6, n7404_1_p2, Y2, n7408_2_p9, n7408_2_p9, n7474_1_p2, n7408_2_p12
  // _7432 7432_2: pin names not known; wires that end beside it: n7404_1_p4, Y2, n7474_1_p2, Y1, n7404_1_p6, X, n7404_1_p2, Y0, n7408_2_p12, n7408_2_p6, n7432_2_p11, n7432_2_p11, n7432_1_p6, n7474_1_p3
endmodule
