// Logisim project Vending machine.circ as structural Verilog: 1 circuit, main circuit main
module main (
  input  x1,
  input  x2,
  output Y1,
  output Y2,
  output Z1_Drink,
  output Z2_Change
);

  wire clock_1_out, n7404_1_p3, n7404_1_p5, n7404_1_p7, n7404_1_p9, n7408_1_p3, n7408_1_p6, n7408_1_p8,
       n7408_1_p11, n7408_1_p14, n7408_2_p9, n7408_2_p10, n7408_2_p13, n7408_3_p7, n7408_4_p4, n7408_5_p7,
       n7432_1_p1, n7432_1_p2, n7432_1_p3, n7432_1_p5, n7432_1_p6, n7432_1_p8, n7432_1_p9, n7432_2_p1,
       n7432_2_p2, n7432_2_p3, n7432_2_p4, n7432_2_p5, n7432_2_p6, n7432_2_p9, n7432_3_p1, n7432_3_p2,
       n7432_3_p3, n7432_3_p5, n7474_1_p6, n7474_1_p7;

  // _7404 7404_1: pin names not known; wires that end beside it: 1'b0, x1, n7404_1_p3, x2, n7404_1_p5, Y1, n7404_1_p7, Y2, n7404_1_p9
  Clock clock_1 (.out(clock_1_out));
  // _7408 7408_1: pin names not known; wires that end beside it: n7404_1_p7, Y2, n7408_1_p3, n7404_1_p7, n7404_1_p9, n7408_1_p6, 1'b0, n7408_1_p8, Y1, Y2, n7408_1_p11, Y1, n7404_1_p9, n7408_1_p14, n7408_1_p8
  // _7432 7432_1: pin names not known; wires that end beside it: n7432_1_p1, n7432_1_p2, n7432_1_p3, 1'b0, n7432_1_p5, n7432_1_p6, n7432_1_p1, n7432_1_p8, n7432_1_p9, n7432_1_p2
  // _7474 7474_1: pin names not known; wires that end beside it: n7432_1_p3, clock_1_out, Y1, n7404_1_p7, 1'b0, n7474_1_p6, n7474_1_p7, clock_1_out, Y2, n7404_1_p9, n7474_1_p6
  // _7408 7408_2: pin names not known; wires that end beside it: n7408_1_p6, n7404_1_p3, n7408_1_p3, n7432_1_p8, x2, n7408_1_p14, n7432_1_p9, 1'b0, n7408_2_p9, n7408_2_p10, n7404_1_p7, n7432_1_p5, n7408_2_p13, Y1, n7432_1_p6, n7408_2_p9
  // _7432 7432_2: pin names not known; wires that end beside it: n7432_2_p1, n7432_2_p2, n7432_2_p3, n7432_2_p4, n7432_2_p5, n7432_2_p6, n7432_2_p6, n7408_2_p13, n7432_2_p9
  // _7432 7432_3: pin names not known; wires that end beside it: n7432_3_p1, n7432_3_p2, n7432_3_p3, n7432_3_p3, n7432_3_p5, n7474_1_p7
  // _7408 7408_3: pin names not known; wires that end beside it: n7408_2_p13, Y2, n7432_3_p5, n7408_2_p10, Y2, n7432_3_p1, n7408_3_p7, n7404_1_p9, n7432_3_p2
  // _7408 7408_4: pin names not known; wires that end beside it: n7408_1_p11, n7404_1_p3, n7432_2_p5, n7408_4_p4, Y1, n7432_2_p1, n7408_2_p10, Y1, n7432_2_p4, n7408_4_p4, Y2, n7432_2_p2
  // _7408 7408_5: pin names not known; wires that end beside it: x1, x2, n7408_2_p13, x1, n7404_1_p5, n7408_4_p4, n7408_5_p7, n7404_1_p3, x2, n7408_3_p7, n7404_1_p3, n7404_1_p5, n7408_2_p10, n7408_5_p7
  // _7474 7474_2: pin names not known; wires that end beside it: n7432_2_p9, clock_1_out, Z1_Drink, n7432_2_p3, clock_1_out, Z2_Change

  // Notes on the sheet:
  //   Y1
  //   Y2
  //   y1y2
  //   y1~y2
  //   ~y1Y2
  //   ~y1~y2
  //   x1x2
  //   ~x1x2
  //   x1 ~x2
  //   ~x1~x2
endmodule
