// Logisim project Sequence Detector 10110.circ as structural Verilog: 1 circuit, main circuit main
module main (
  input  X,
  output Y2,
  output Y1,
  output Y0,
  output Z
);

  wire clock_1_out, n7404_1_p2, n7408_1_p9, n7408_1_p12, n7408_3_p9, n7432_1_p1, n7432_1_p2, n7432_1_p3,
       n7432_1_p5, n7432_1_p7, n7432_2_p1, n7432_2_p2, n7432_2_p3, n7432_2_p5, n7474_1_p4, n7474_1_p5,
       n7474_2_p5;

  Clock clock_1 (.out(clock_1_out));
  // _7404 7404_1: pin names not known; wires that end beside it: X, n7404_1_p2
  // _7432 7432_1: pin names not known; wires that end beside it: n7432_1_p1, n7432_1_p2, n7432_1_p3, Y1, n7432_1_p5, Y2, n7432_1_p7
  // _7474 7474_1: pin names not known; wires that end beside it: n7432_1_p3, clock_1_out, Y0, n7474_1_p4, n7474_1_p5, clock_1_out, Y1, n7432_1_p5
  // _7408 7408_1: pin names not known; wires that end beside it: X, n7432_1_p5, n7432_1_p1, X, n7474_1_p4, n7432_1_p2, X, Y1, n7408_1_p9, n7408_1_p9, Y0, n7408_1_p12
  // _7474 7474_2: pin names not known; wires that end beside it: n7408_1_p12, clock_1_out, Y2, n7432_1_p7, n7474_2_p5, clock_1_out, Z
  // _7408 7408_2: pin names not known; wires that end beside it: n7404_1_p2, Y2, n7474_2_p5
  // _7432 7432_2: pin names not known; wires that end beside it: n7432_2_p1, n7432_2_p2, n7432_2_p3, n7432_2_p3, n7432_2_p5, n7474_1_p5
  // _7408 7408_3: pin names not known; wires that end beside it: n7404_1_p2, Y0, n7432_2_p1, n7404_1_p2, Y2, n7432_2_p2, X, Y1, n7408_3_p9, n7408_3_p9, n7474_1_p4, n7432_2_p5, Y0, Y1, n7432_1_p5, Y2, n7432_1_p7, X, n7404_1_p2
endmodule
