// Logisim project Sequence Detector.circ as structural Verilog: 1 circuit, main circuit main
module main (
  input  x,
  output Y1,
  output Y0,
  output Z
);

  wire clk_out, n7404_1_p2, n7408_1_p1, n7408_2_p3, n7432_1_p1, n7432_1_p2, n7432_1_p3, n7474_1_p4;

  Clock clk (.out(clk_out));
  // _7404 7404_1: pin names not known; wires that end beside it: x, n7404_1_p2
  // _7432 7432_1: pin names not known; wires that end beside it: n7432_1_p1, n7432_1_p2, n7432_1_p3
  // _7474 7474_1: pin names not known; wires that end beside it: n7404_1_p2, clk_out, Y0, n7474_1_p4, n7432_1_p3, clk_out, Y1
  // _7408 7408_1: pin names not known; wires that end beside it: n7408_1_p1, Y1, n7432_1_p2, x, Y0, n7432_1_p1, n7404_1_p2, n7474_1_p4, n7408_1_p1, n7404_1_p2
  // _7408 7408_2: pin names not known; wires that end beside it: x, Y0, n7408_2_p3, n7408_2_p3, Y1, Z

  // Notes on the sheet:
  //   1010 sequence detector
endmodule
