// Logisim project Vending Machine.circ as structural Verilog: 1 circuit, main circuit main
module main (
  input  x1,
  input  x2,
  output Change,
  output Candy_Output
);

  wire clock_1_out, n7408_1_p1, n7408_1_p2, n7408_1_p3, n7408_1_p4, n7408_1_p5, n7408_1_p7, n7408_2_p9,
       n7408_2_p12, n7476_1_p4, n7476_1_p7;

  Clock clock_1 (.out(clock_1_out));
  // _7408 7408_1: pin names not known; wires that end beside it: n7408_1_p1, n7408_1_p2, n7408_1_p3, n7408_1_p4, n7408_1_p5, x1, n7408_1_p7
  // _7476 7476_1: pin names not known; wires that end beside it: clock_1_out, x1, clock_1_out, n7476_1_p4, n7408_1_p1, n7408_1_p2, n7476_1_p7, n7408_1_p3, n7408_1_p4, n7476_1_p7
  // _7408 7408_2: pin names not known; wires that end beside it: n7408_1_p1, n7408_1_p3, n7408_1_p5, n7408_1_p5, x2, Change, x2, n7408_1_p3, n7408_2_p9, x1, n7408_1_p1, n7408_2_p12
  // _7432 7432_1: pin names not known; wires that end beside it: n7408_2_p9, x1, n7476_1_p4, n7408_2_p12, x2, n7476_1_p7, n7408_1_p7, n7408_2_p9, Candy_Output, n7408_1_p1, n7408_1_p2
endmodule
