// Logisim project Digital Lock.circ as structural Verilog: 1 circuit, main circuit main
module main (
  input  in_1,
  input  in_2,
  input  in_3,
  input  in_4,
  input  in_5,
  output out_6,
  output out_7,
  output out_8
);

  Button x1 ();  // open: out
  Button x2 ();  // open: out
  Button x3 (.out(out_7));
  // _7476 7476_1: pin names not known; wires that end beside it: in_1, in_2, in_3, out_6
  S_R_Flip_Flop s_r_ff_1 (.S(in_4), .R(in_5), .Q(out_8));  // open: clk, Qn, preset, reset, en
endmodule
