// Logisim project Nelso Exercise 10.9.circ as structural Verilog: 1 circuit, main circuit main
module main (
  input  x1,
  input  x2,
  output out_3
);

  wire and_1_out, and_2_out, and_3_out, and_4_out, and_5_out, n74116_1_p4, or_1_out;

  and and_1 (and_1_out, x1, x2);
  and and_2 (and_2_out, x2, n74116_1_p4);
  and and_3 (and_3_out, n74116_1_p4, x1);
  or or_1 (or_1_out, and_1_out, and_2_out, and_3_out);
  // _74116 74116_1: pin names not known; wires that end beside it: 1'b0, 1'b0, or_1_out, n74116_1_p4, 1'b0
  and and_4 (and_4_out, ~n74116_1_p4, ~x1, x2);  // AND_Gate
  and and_5 (and_5_out, n74116_1_p4, x1, ~x2);  // AND_Gate
  or or_2 (out_3, and_4_out, and_5_out);
endmodule
