// Logisim project Nelson 10.9.circ as structural Verilog
module main (
  input  x1,
  input  x2,
  output y,
  output z
);

  wire n7404_1_p2, n7404_1_p4, n7404_1_p6, n7408_2_p3, n7408_3_p3, n7432_1_p1, n7432_1_p2, n7432_1_p3,
       n7432_1_p5, n7432_1_p6, n7432_2_p1, n7432_2_p2;

  // _7404 7404_1: pin names not known; wires that end beside it: y, n7404_1_p2, x2, n7404_1_p4, x1, n7404_1_p6
  // _7432 7432_1: pin names not known; wires that end beside it: n7432_1_p1, n7432_1_p2, n7432_1_p3, n7432_1_p3, n7432_1_p5, n7432_1_p6
  // _7408 7408_1: pin names not known; wires that end beside it: y, x2, n7432_1_p2, y, x1, n7432_1_p1, x1, x2, n7432_1_p5
  // _7432 7432_2: pin names not known; wires that end beside it: n7432_2_p1, n7432_2_p2, z
  // _7408 7408_2: pin names not known; wires that end beside it: n7404_1_p2, n7404_1_p6, n7408_2_p3, n7408_2_p3, x2, n7432_2_p1
  // _7408 7408_3: pin names not known; wires that end beside it: y, x1, n7408_3_p3, n7408_3_p3, n7404_1_p4, n7432_2_p2
  // _74116 74116_1: pin names not known; wires that end beside it: 1'b0, 1'b0, n7432_1_p6, y

  // Notes on the sheet:
  //   x1'
  //   y'
  //   x1
  //   yx2
  //   yx1
  //   x2
  //   x1x2
  //   y'x1'x2
  //   yx1x2'
endmodule

module sr_latch_nelson_10_9 (
  input  x1,
  input  x2,
  output y,
  output z
);

  wire n7402_1_p1, n7402_1_p2, n7402_1_p6, n7404_1_p2, n7404_1_p4, n7408_2_p3, n7408_2_p6, n7408_2_p9,
       n7408_2_p12;

  // _7402 7402_1: pin names not known; wires that end beside it: n7402_1_p1, n7402_1_p2, y, y, n7402_1_p1, n7402_1_p6
  // _7404 7404_1: pin names not known; wires that end beside it: x1, n7404_1_p2, x2, n7404_1_p4
  // _7408 7408_1: pin names not known; wires that end beside it: x1, x2, n7402_1_p2, n7404_1_p2, n7404_1_p4, n7402_1_p6
  // _7408 7408_2: pin names not known; wires that end beside it: n7402_1_p1, x2, n7408_2_p3, n7408_2_p3, n7404_1_p2, n7408_2_p6, y, n7404_1_p4, n7408_2_p9, n7408_2_p9, x1, n7408_2_p12
  // _7432 7432_1: pin names not known; wires that end beside it: n7408_2_p12, n7408_2_p6, z
  // _7408 7408_3: pin names not known

  // Notes on the sheet:
  //   y'
  //   s
  //   r
  //   x1'
  //   x2'
  //   y'x1'x2
  //   yx1x2'
endmodule
