// Logisim project Nelson Example 10.7.circ as structural Verilog: 2 circuits, main circuit main
module main (
  input  x1,
  input  x2,
  output z1,
  output z1_2
);

  wire and_1_out, and_2_out, and_3_out, and_4_out, and_5_out, and_6_out, and_7_out, n74116_1_p4, n74116_1_p6,
       or_1_out, or_2_out;

  and and_1 (and_1_out, n74116_1_p4, n74116_1_p6);
  and and_2 (and_2_out, x1, n74116_1_p4);
  and and_3 (and_3_out, ~x2, n74116_1_p4);  // AND_Gate
  and and_4 (and_4_out, x1, ~x2, ~n74116_1_p6);  // AND_Gate
  and and_5 (and_5_out, x1, x2);
  and and_6 (and_6_out, x1, n74116_1_p6);
  and and_7 (and_7_out, x2, n74116_1_p6);
  or or_1 (or_1_out, and_1_out, and_2_out, and_3_out, and_4_out);
  or or_2 (or_2_out, and_5_out, and_6_out, and_7_out);
  // _74116 74116_1: pin names not known; wires that end beside it: 1'b0, 1'b0, or_1_out, n74116_1_p4, or_2_out, n74116_1_p6, 1'b0, or_2_out, n74116_1_p4
  and and_8 (z1, ~n74116_1_p4, n74116_1_p6);  // AND_Gate
  and and_9 (z1_2, n74116_1_p4, n74116_1_p6);
endmodule

module my_solve (
  input  x1,
  input  x2,
  output z1,
  output z1_2
);

  wire and_1_out, and_2_out, and_3_out, and_4_out, and_5_out, and_6_out, n74116_1_p4, n74116_1_p6, or_1_out,
       or_2_out;

  and and_1 (and_1_out, x2, n74116_1_p4);
  and and_2 (and_2_out, x1, x2);
  and and_3 (and_3_out, x1, n74116_1_p4);
  and and_4 (and_4_out, x1, ~n74116_1_p4, ~n74116_1_p6);  // AND_Gate
  and and_5 (and_5_out, n74116_1_p6, x1, ~x2);  // AND_Gate
  and and_6 (and_6_out, n74116_1_p4, n74116_1_p6, x2);
  or or_1 (or_1_out, and_1_out, and_2_out, and_3_out);
  or or_2 (or_2_out, and_4_out, and_5_out, and_6_out);
  // _74116 74116_1: pin names not known; wires that end beside it: 1'b0, 1'b0, or_1_out, n74116_1_p4, or_2_out, n74116_1_p6, 1'b0, or_2_out, n74116_1_p4
  and and_7 (z1, n74116_1_p4, n74116_1_p6);
  and and_8 (z1_2, n74116_1_p4, ~n74116_1_p6);  // AND_Gate
endmodule
