// Logisim project 1805022.circ as structural Verilog: 1 circuit, main circuit main
module main (
  input  A,
  input  B,
  input  C,
  input  D,
  output out_5
);

  wire n7404_1_p2, n7404_1_p4, n7404_1_p12, n7404_1_p14, n7408_1_p3, n7408_1_p6, n7408_1_p11, n7408_1_p14,
       n7432_1_p5, n7432_1_p8, n7432_1_p9, n7432_1_p10;

  // _7404 7404_1: pin names not known; wires that end beside it: A, n7404_1_p2, B, n7404_1_p4, A, n7404_1_p2, B, n7404_1_p4, 1'b0, 1'b1, C, n7404_1_p12, D, n7404_1_p14, C
  // _7408 7408_1: pin names not known; wires that end beside it: n7404_1_p4, n7404_1_p14, n7408_1_p3, n7408_1_p3, n7404_1_p12, n7408_1_p6, 1'b0, 1'b1, n7404_1_p2, C, n7408_1_p11, n7408_1_p11, D, n7408_1_p14
  // _7432 7432_1: pin names not known; wires that end beside it: D, n7404_1_p14, n7408_1_p6, n7408_1_p14, n7432_1_p5, 1'b0, 1'b1, n7432_1_p8, n7432_1_p9, n7432_1_p10, n7432_1_p10, n7432_1_p5, out_5
  // _7408 7408_2: pin names not known; wires that end beside it: n7408_1_p11, B, n7432_1_p9, n7408_1_p3, A, n7432_1_p8, 1'b0, 1'b1
endmodule
