// Logisim project A1B1.circ as structural Verilog
module _5 (
  input  A,
  input  B,
  input  C,
  input  D,
  output out_5
);

  wire n7404_1_p2, n7404_1_p4, n7404_1_p8, n7404_1_p10, n7408_1_p3, n7408_1_p6, n7408_1_p10, n7408_2_p4,
       n7408_2_p7, n7408_3_p7, n7408_3_p10, n7408_3_p15, n7432_1_p3;

  // _7404 7404_1: pin names not known; wires that end beside it: A, n7404_1_p2, B, n7404_1_p4, 1'b0, 1'b1, C, n7404_1_p8, D, n7404_1_p10
  // _7408 7408_1: pin names not known; wires that end beside it: n7404_1_p2, B, n7408_1_p3, C, n7404_1_p10, n7408_1_p6, 1'b1, n7408_1_p3, n7408_1_p6, n7408_1_p10
  // _7408 7408_2: pin names not known; wires that end beside it: 1'b0, A, n7404_1_p4, n7408_2_p4, n7408_2_p4, D, n7408_2_p7, 1'b0, 1'b1
  // _7408 7408_3: pin names not known; wires that end beside it: C, n7404_1_p8, D, n7404_1_p10, A, B, n7408_3_p7, n7404_1_p8, n7404_1_p10, n7408_3_p10, 1'b0, 1'b1, n7408_3_p7, n7408_3_p10, n7408_3_p15
  // _7432 7432_1: pin names not known; wires that end beside it: n7408_1_p10, n7408_2_p7, n7432_1_p3, n7432_1_p3, n7408_3_p15, out_5
endmodule

module _1 (
  input  A,
  input  B,
  input  C,
  input  D,
  output Y
);

  wire n7408_1_p3, n7408_1_p6, n7408_1_p11, n7408_1_p14, n7408_2_p7, n7408_2_p10, n7408_2_p15, n7408_2_p18,
       n7432_1_p3, n7432_1_p6, NOT_p3, NOT_p5, NOT_p7, NOT_p9;

  // _7404 NOT: pin names not known; wires that end beside it: 1'b0, A, NOT_p3, B, NOT_p5, C, NOT_p7, D, NOT_p9
  // _7408 7408_1: pin names not known; wires that end beside it: NOT_p3, NOT_p7, n7408_1_p3, n7408_1_p3, D, n7408_1_p6, 1'b0, 1'b1, NOT_p3, C, n7408_1_p11, n7408_1_p11, NOT_p9, n7408_1_p14
  // _7408 7408_2: pin names not known; wires that end beside it: C, NOT_p7, D, NOT_p9, B, NOT_p7, n7408_2_p7, n7408_2_p7, NOT_p9, n7408_2_p10, 1'b0, 1'b1, A, NOT_p5, n7408_2_p15, n7408_2_p15, D, n7408_2_p18
  // _7432 7432_1: pin names not known; wires that end beside it: n7408_1_p6, n7408_1_p14, n7432_1_p3, n7408_2_p10, n7408_2_p18, n7432_1_p6, 1'b0, 1'b1, n7432_1_p3, n7432_1_p6, Y, 1'b1
endmodule
