// Logisim project A2B2.circ as structural Verilog
module _1 (
  input  A,
  input  B,
  input  C,
  input  D,
  output out_5
);

  wire n7408_1_p3, n7408_1_p6, n7408_1_p11, n7408_1_p14, n7408_2_p7, n7408_2_p10, n7408_2_p15, n7408_2_p18,
       n7432_1_p3, n7432_1_p6, NOT_p3, NOT_p5, NOT_p9, NOT_p11;

  // _7404 NOT: pin names not known; wires that end beside it: 1'b0, A, NOT_p3, B, NOT_p5, 1'b0, 1'b1, C, NOT_p9, D, NOT_p11
  // _7408 7408_1: pin names not known; wires that end beside it: NOT_p5, NOT_p9, n7408_1_p3, n7408_1_p3, D, n7408_1_p6, 1'b0, 1'b1, NOT_p5, C, n7408_1_p11, n7408_1_p11, NOT_p11, n7408_1_p14
  // _7408 7408_2: pin names not known; wires that end beside it: C, NOT_p9, D, NOT_p11, NOT_p3, B, n7408_2_p7, n7408_2_p7, NOT_p9, n7408_2_p10, 1'b0, 1'b1, B, NOT_p9, n7408_2_p15, n7408_2_p15, NOT_p11, n7408_2_p18
  // _7432 7432_1: pin names not known; wires that end beside it: n7408_1_p6, n7408_1_p14, n7432_1_p3, n7408_2_p18, n7408_2_p10, n7432_1_p6, 1'b0, 1'b1, n7432_1_p3, n7432_1_p6, out_5, 1'b1
endmodule

module _5 (
  input  A,
  input  B,
  input  C,
  input  D,
  output out_5
);

  wire n7408_1_p3, n7408_1_p6, n7408_1_p11, n7408_1_p14, n7408_2_p7, n7408_2_p10, n7408_2_p15, n7408_2_p18,
       n7432_1_p3, n7432_1_p6, NOT_p3, NOT_p5, NOT_p9, NOT_p11;

  // _7404 NOT: pin names not known; wires that end beside it: 1'b0, A, NOT_p3, B, NOT_p5, 1'b0, 1'b1, C, NOT_p9, D, NOT_p11
  // _7408 7408_1: pin names not known; wires that end beside it: NOT_p5, C, n7408_1_p3, n7408_1_p3, NOT_p11, n7408_1_p6, 1'b0, 1'b1, NOT_p3, B, n7408_1_p11, n7408_1_p11, D, n7408_1_p14
  // _7408 7408_2: pin names not known; wires that end beside it: C, NOT_p9, D, NOT_p11, A, C, n7408_2_p7, n7408_2_p7, NOT_p11, n7408_2_p10, 1'b0, 1'b1, B, NOT_p9, n7408_2_p15, n7408_2_p15, D, n7408_2_p18
  // _7432 7432_1: pin names not known; wires that end beside it: n7408_1_p6, n7408_1_p14, n7432_1_p3, n7408_2_p10, n7408_2_p18, n7432_1_p6, 1'b0, 1'b1, n7432_1_p3, n7432_1_p6, out_5, 1'b1
endmodule
