// Logisim project Group_5_Problem_1.circ as structural Verilog: 1 circuit, main circuit main
module main (
  input  B,
  input  D,
  output out_3
);

  wire n7404_1_p2, n7404_1_p4, n7408_1_p3, n7408_1_p6;

  // _7404 7404_1: pin names not known; wires that end beside it: B, n7404_1_p2, D, n7404_1_p4, B
  // _7408 7408_1: pin names not known; wires that end beside it: n7404_1_p2, n7404_1_p4, n7408_1_p3, B, D, n7408_1_p6
  // _7432 7432_1: pin names not known; wires that end beside it: n7408_1_p3, n7408_1_p6, out_3
endmodule
