// Logisim project Group_5_Problem_2.circ as structural Verilog: 1 circuit, main circuit main
module main (
  input  A,
  input  B,
  input  C,
  output X,
  output Z,
  output Y
);

  wire n7404_1_p2, n7404_1_p4, n7404_1_p6, n7408_1_p3, n7408_1_p6, n7408_1_p8, n7408_1_p9, n7408_2_p4,
       n7432_1_p5, n7432_1_p6, n7432_1_p8, n7432_1_p9, n7432_1_p11;

  // _7404 7404_1: pin names not known; wires that end beside it: A, n7404_1_p2, B, n7404_1_p4, C, n7404_1_p6
  // _7408 7408_1: pin names not known; wires that end beside it: n7404_1_p2, B, n7408_1_p3, n7404_1_p4, A, n7408_1_p6, C, n7408_1_p8, n7408_1_p9, n7404_1_p2, n7404_1_p4, n7408_1_p8
  // _7432 7432_1: pin names not known; wires that end beside it: n7408_1_p3, n7408_1_p6, Y, n7408_1_p9, n7432_1_p5, n7432_1_p6, n7432_1_p6, n7432_1_p8, n7432_1_p9, n7432_1_p9, n7432_1_p11, Z
  // _7408 7408_2: pin names not known; wires that end beside it: C, A, B, n7408_2_p4, n7408_2_p4, C, n7432_1_p5, n7408_1_p3, n7404_1_p6, n7432_1_p8, n7408_1_p6, n7404_1_p6, n7432_1_p11

  assign X = A;
endmodule
