// Logisim project Group_5_problem_3.circ as structural Verilog: 1 circuit, main circuit main
module main (
  input  A,
  input  B,
  input  C,
  output X,
  output Y
);

  wire n7404_1_p2, n7404_1_p4, n7404_1_p6, n7408_1_p3, n7408_1_p6, n7408_1_p9, n7408_1_p12, n7408_2_p4,
       n7408_2_p5, n7408_3_p1, n7408_3_p3, n7408_3_p7, n7408_3_p9, n7408_3_p10, n7432_1_p2, n7432_2_p3,
       n7432_2_p6;

  // _7404 7404_1: pin names not known; wires that end beside it: B, n7404_1_p2, A, n7404_1_p4, C, n7404_1_p6
  // _7408 7408_1: pin names not known; wires that end beside it: C, A, n7408_1_p3, A, B, n7408_1_p6, n7404_1_p2, n7404_1_p6, n7408_1_p9, C, B, n7408_1_p12
  // _7432 7432_1: pin names not known; wires that end beside it: n7408_1_p3, n7432_1_p2, X, n7408_1_p12, n7408_1_p6, n7432_1_p2
  // _7408 7408_2: pin names not known; wires that end beside it: A, n7408_1_p9, A, n7408_2_p4, n7408_2_p5, C, B, n7408_2_p4
  // _7408 7408_3: pin names not known; wires that end beside it: n7408_3_p1, C, n7408_3_p3, n7404_1_p4, n7404_1_p2, n7408_3_p1, n7408_3_p7, n7404_1_p6, n7408_3_p9, n7408_3_p10, B, n7404_1_p4, n7408_3_p9
  // _7432 7432_2: pin names not known; wires that end beside it: n7408_3_p10, n7408_3_p3, n7432_2_p3, n7432_2_p3, n7408_3_p7, n7432_2_p6, n7408_2_p5, n7432_2_p6, Y
endmodule
