// Logisim project Group_5_problem_4.circ as structural Verilog: 1 circuit, main circuit main
module main (
  input  A,
  input  B,
  input  C,
  input  D,
  output out_5
);

  wire n7404_1_p2, n7404_1_p4, n7404_1_p6, n7404_1_p8, n7408_1_p3, n7408_1_p6, n7408_1_p9, n7408_1_p12,
       n7408_2_p3, n7408_2_p6, n7408_2_p9, n7408_2_p12, n7408_3_p3, n7408_3_p6, n7408_3_p8, n7408_3_p9,
       n7432_1_p3, n7432_1_p6;

  // _7404 7404_1: pin names not known; wires that end beside it: A, n7404_1_p2, B, n7404_1_p4, D, n7404_1_p6, C, n7404_1_p8
  // _7408 7408_1: pin names not known; wires that end beside it: n7404_1_p2, B, n7408_1_p3, n7408_1_p3, C, n7408_1_p6, n7404_1_p4, A, n7408_1_p9, n7404_1_p6, n7408_1_p6, n7408_1_p12
  // _7408 7408_2: pin names not known; wires that end beside it: A, B, n7408_2_p3, n7408_1_p9, n7404_1_p8, n7408_2_p6, n7408_2_p3, n7404_1_p8, n7408_2_p9, D, n7408_2_p6, n7408_2_p12
  // _7408 7408_3: pin names not known; wires that end beside it: n7408_2_p9, n7404_1_p6, n7408_3_p3, A, B, n7408_3_p6, D, n7408_3_p8, n7408_3_p9, C, n7408_3_p6, n7408_3_p8
  // _7432 7432_1: pin names not known; wires that end beside it: n7408_1_p12, n7408_2_p12, n7432_1_p3, n7408_3_p3, n7432_1_p3, n7432_1_p6, n7432_1_p6, n7408_3_p9, out_5
endmodule
