// Logisim project 1805022_Q2.circ as structural Verilog
module _2 (
  input  P,
  input  Q,
  input  R,
  input  S,
  output Z
);

  wire NOT_p3, NOT_p5, NOT_p7, NOT_p9;

  // _7404 NOT: pin names not known; wires that end beside it: 1'b0, P, NOT_p3, Q, NOT_p5, S, NOT_p7, R, NOT_p9
  // _7432 7432_1: pin names not known; wires that end beside it: S, NOT_p7, Q, NOT_p7, Z, 1'b0, 1'b1, 1'b1
endmodule
