// Logisim project Group_A1_5_Problem_1.circ as structural Verilog: 1 circuit, main circuit main
module main (
  input  P,
  input  Q,
  input  R,
  input  S,
  output A,
  output B,
  output C
);

  wire n7404_1_p2, n7404_1_p4, n7404_1_p6, n7404_1_p8, n7404_1_p9, n7408_1_p3, n7408_1_p8, n7408_1_p11,
       n7408_2_p3, n7408_2_p6, n7408_2_p9, n7408_2_p12, n7408_3_p6, n7408_3_p8, n7408_3_p9, n7408_4_p3,
       n7408_4_p6, n7432_1_p3, n7432_1_p9, n7432_1_p12, n7432_2_p2;

  // _7404 7404_1: pin names not known; wires that end beside it: Q, n7404_1_p2, S, n7404_1_p4, P, n7404_1_p6, R, n7404_1_p8, n7404_1_p9
  // _7408 7408_1: pin names not known; wires that end beside it: n7404_1_p6, R, n7408_1_p3, n7404_1_p2, S, n7404_1_p6, n7404_1_p9, n7408_1_p8, R, n7404_1_p9, n7408_1_p11
  // _7408 7408_2: pin names not known; wires that end beside it: n7404_1_p6, n7404_1_p8, n7408_2_p3, R, P, n7408_2_p6, n7404_1_p2, n7404_1_p4, n7408_2_p9, S, Q, n7408_2_p12
  // _7432 7432_1: pin names not known; wires that end beside it: n7408_1_p3, n7408_1_p11, n7432_1_p3, n7432_1_p3, n7408_1_p8, A, n7408_2_p9, n7408_2_p12, n7432_1_p9, n7408_2_p3, n7408_2_p6, n7432_1_p12
  // _7408 7408_3: pin names not known; wires that end beside it: n7432_1_p9, n7432_1_p12, B, P, n7404_1_p8, n7408_3_p6, n7404_1_p4, n7408_3_p8, n7408_3_p9, n7404_1_p8, Q, n7408_3_p8
  // _7408 7408_4: pin names not known; wires that end beside it: Q, P, n7408_4_p3, n7408_4_p3, n7404_1_p4, n7408_4_p6
  // _7432 7432_2: pin names not known; wires that end beside it: n7408_3_p9, n7432_2_p2, C, n7408_3_p6, n7408_4_p6, n7432_2_p2
endmodule
