// Logisim project Problem_2_Basic_Implementation.circ as structural Verilog: 1 circuit, main circuit main
module main (
  input  P,
  input  Q,
  input  R,
  output D,
  output B
);

  wire and_1_out, and_2_out, and_3_out, not_1_out, or_1_out, xor_1_out;

  not not_1 (not_1_out, P);
  xor xor_1 (xor_1_out, P, Q);
  and and_1 (and_1_out, not_1_out, R);
  and and_2 (and_2_out, Q, R);
  and and_3 (and_3_out, not_1_out, Q);
  xor xor_2 (D, xor_1_out, R);
  or or_1 (or_1_out, and_1_out, and_2_out);
  or or_2 (B, or_1_out, and_3_out);
endmodule
