// Logisim project Group_A1_5_Problem_2.circ as structural Verilog: 1 circuit, main circuit main
module main (
  input  Q,
  input  R,
  input  P,
  output D,
  output B
);

  wire n7404_1_p2, n7408_1_p3, n7408_1_p6, n7408_1_p9, n7432_1_p3, n7486_1_p3;

  // _7404 7404_1: pin names not known; wires that end beside it: P, n7404_1_p2
  // _7486 7486_1: pin names not known; wires that end beside it: P, Q, n7486_1_p3, n7486_1_p3, R, D
  // _7408 7408_1: pin names not known; wires that end beside it: n7404_1_p2, R, n7408_1_p3, Q, R, n7408_1_p6, n7404_1_p2, Q, n7408_1_p9
  // _7432 7432_1: pin names not known; wires that end beside it: n7408_1_p9, n7408_1_p6, n7432_1_p3, n7432_1_p3, n7408_1_p3, B
endmodule
