// Logisim project 1805022.circ as structural Verilog: 1 circuit, main circuit main
module main (
  input  [3:0] in_1,
  input  in_2,
  input  in_3,
  output out_4
);

  wire n74153_1_p4, n74153_1_p7, n74153_1_p13, n74153_1_p16;

  // _74153 74153_1: pin names not known; wires that end beside it: in_3, in_1[2], in_1[0], n74153_1_p4, in_3, in_3, n74153_1_p7, 1'b0, 1'b1, in_2, in_1[1], in_2, n74153_1_p13, n74153_1_p4, in_1[0], n74153_1_p16
  // _74157 74157_1: pin names not known; wires that end beside it: in_3, in_1[3], n74153_1_p7, n74153_1_p16, out_4, 1'b0, 1'b1, in_2, in_1[0], n74153_1_p4, n74153_1_p13, in_2
  // _7404 7404_1: pin names not known; wires that end beside it: in_1[0], n74153_1_p4, 1'b0, 1'b1, in_2, n74153_1_p13
endmodule
