// Logisim project encoderExample.circ as structural Verilog: 2 circuits, main circuit main
module main (
  input  _0,
  input  _1,
  input  _2,
  input  _3,
  input  _4,
  input  _5,
  input  _6,
  input  _7,
  input  _8,
  output A0,
  output A1,
  output A2,
  output A3
);

  // _7400_lib_74147 74147_1: pin names not known; wires that end beside it: _3, _4, _5, _6, _7, A2, A1, 1'b0, A3, _2, _1, _0, _8, A0
endmodule

module _74147 (
  input  _0,
  input  _1,
  input  _2,
  input  _3,
  input  _4,
  input  _5,
  input  _6,
  input  _7,
  input  _8,
  output A0,
  output A1,
  output A2,
  output A3
);

  // _7400_lib_74147 74147_1: pin names not known; wires that end beside it: _3, _4, _5, _6, _7, A2, A1, 1'b0, A3, _2, _1, _0, _8, A0
endmodule
