// Logisim project online.circ as structural Verilog: 1 circuit, main circuit main
module main (
  input  D3,
  input  D2,
  input  D1,
  input  D0,
  output Y0,
  output Y1
);

  wire AND_p3, AND_p6, NOT_p5, NOT_p7;

  // _7404 NOT: pin names not known; wires that end beside it: D2, 1'b0, 1'b1, D1, NOT_p5, D0, NOT_p7
  // _7408 AND: pin names not known; wires that end beside it: NOT_p7, D1, AND_p3, D3, NOT_p7, AND_p6, 1'b0, 1'b1, NOT_p7, NOT_p5, Y1, 1'b0
  // _7432 OR: pin names not known; wires that end beside it: AND_p3, AND_p6, Y0, 1'b1
endmodule
