// Logisim project mux.circ as structural Verilog: 3 circuits, main circuit main
module main (
  input  in_1,
  input  [27:0] X,
  input  [27:0] Y,
  output [27:0] Y_2
);

  wire [3:0] n74157_1_p4;

  // _74157 74157_1: pin names not known; wires that end beside it: in_1, X[0], Y[0], n74157_1_p4[0], X[1], Y[1], n74157_1_p4[1], 1'b0, 1'b1, 1'b0, X[3], Y[3], n74157_1_p4[3], X[2], Y[2], n74157_1_p4[2]
  // _74157 74157_2: pin names not known; wires that end beside it: in_1, X[4], Y[4], X[5], Y[5], X[7], X[6]
  Mux mux_1 (.in_1(in_1), .X(X), .Y(Y), .X_2(Y_2));
endmodule

module SubMux4 (
  input  S,
  input  [3:0] X,
  input  [3:0] Y,
  output [3:0] Z
);

  // _74157 74157_1: pin names not known; wires that end beside it: S, X[0], Y[0], Z[0], X[1], Y[1], Z[1], 1'b0, 1'b1, 1'b0, X[3], Y[3], Z[3], X[2], Y[2], Z[2]
endmodule

module Mux (
  input  in_1,
  input  [27:0] X,
  input  [27:0] Y,
  output [27:0] X_2
);

  SubMux4 submux4_1 (.S(in_1), .X(X[3:0]), .Y(Y[3:0]), .Z(X_2[3:0]));
  SubMux4 submux4_2 (.S(in_1), .X(X[7:4]), .Y(Y[7:4]), .Z(X_2[7:4]));
  SubMux4 submux4_3 (.S(in_1), .X(X[11:8]), .Y(Y[11:8]), .Z(X_2[11:8]));
  SubMux4 submux4_4 (.S(in_1), .X(X[15:12]), .Y(Y[15:12]), .Z(X_2[15:12]));
  SubMux4 submux4_5 (.S(in_1), .X(X[19:16]), .Y(Y[19:16]), .Z(X_2[19:16]));
  SubMux4 submux4_6 (.S(in_1), .X(X[23:20]), .Y(Y[23:20]), .Z(X_2[23:20]));
  SubMux4 submux4_7 (.S(in_1), .X(X[27:24]), .Y(Y[27:24]), .Z(X_2[27:24]));
endmodule
